# Fritzing sketch potentiometers_various (saved by Fritzing 0.9.3b)
breadboards: 3

parts:
  R1 = TRIMPOT [package=3362u-2]
  R3 = Trimmer Potentiometer [maximum_resistance=10kΩ package=THT]
  U1 = POT [package=pot_alpha_rv16af-20]
  Part1 = Arduino Uno (Rev3)
  Part2 = Arduino Uno (Rev3)
  Part3 = Arduino Uno (Rev3)

nets:
  N1: R1.CCW, Part1.GND
  N2: R1.WIPER, Part1.A0
  N3: R1.CW, Part1.5V
  N4: R3.leg1, Part2.GND
  N5: R3.wiper, Part2.A0
  N6: R3.leg2, Part2.5V
  N7: U1.A, U1.E, Part3.GND
  N8: U1.S, Part3.A0
